# Fritzing sketch schema (saved by Fritzing 0.9.6b)
breadboards: 1

parts:
  U1 = RF-LINK_RX [package=rf-link_rx]
  Composant1 = Arduino Uno (Rev3)

nets:
  GND: U1.GND, Composant1.GND
  N1: U1.Data#3, Composant1.D2
  VCC: U1.VCC, Composant1.5V

custom parts:
  RF-LINK_RX: RF Link receivers- WRL-8947, 8948, 8949, 8950
